# Fritzing sketch AsTra-V0.44 (saved by Fritzing 0.8.7b)
circuit board: 5.5cm x 5.1cm

parts:
  1117-3_3_GND_OUT_IN = V_REG_LD1117VXX [package=78xxl]
  C1 = Tantalum Capacitor [capacitance=1μF package="100 mil [THT, tantalum]"]
  C2 = Tantalum Capacitor [capacitance=1μF package="100 mil [THT, tantalum]"]
  Up = Pushbutton [package="[THT]"]
  I2C_Level_Converter = Logic Level Converter
  DC-DC = NCP1400 Step-Up Breakout
  VCC1 = Battery
  Down = Pushbutton [package="[THT]"]
  Start/Stop = Pushbutton [package="[THT]"]
  Setup = Pushbutton [package="[THT]"]
  R6 = Resistor [tolerance=±5% resistance=100k package=THT]
  R7 = Resistor [tolerance=±5% resistance=10k package=THT]
  R8 = Resistor [tolerance=±5% resistance=10k package=THT]
  R9 = Resistor [tolerance=±5% resistance=10k package=THT]
  Beeper = Piezo Speaker
  LCD_contrast = Trimmer Potentiometer [maximum_resistance=10kΩ package=THT]
  LCD_Connector = LCD Connector [form="♂ (male)" package=THT]
  Arduino_Mini = Arduino Pro Mini v13
  Mode = LED - 3mm [color="Red (660nm)" package="3 mm [THT]"]
  R11 = Resistor [tolerance=±5% resistance=220 package=THT]
  MicroSD_breakout = MicroSD breakout [form="♂ (male)" package=THT]
  RTC = DS1307 RTC Breakout fixsize
  MS5611_breakout = MS5611 breakout CSG [form="♂ (male)" package=THT]
  microSD1 = MicroSD Breakout  # not connected
  R10 = Resistor [tolerance=±5% resistance=10k package=THT]
  Power = female pin header, 4 pins [form="♀ (female)"]
  Keypad = female pin header, 2 pins [form="♀ (female)"]
  R12 = Resistor [tolerance=±5% resistance=470 package=THT]

nets:
  3.3V: 1117-3_3_GND_OUT_IN.OUT, C1.+, I2C_Level_Converter.LV, MS5611_breakout.VDD=3.3V, Power.pin3
  GND: 1117-3_3_GND_OUT_IN.GND, C1.-, C2.-, I2C_Level_Converter.GND, DC-DC.GND, VCC1.-, R6.Pin_0, Beeper.pin2, LCD_contrast.leg1, LCD_Connector.VSS=GND, Arduino_Mini.GND, Mode.cathode, MicroSD_breakout.GND, RTC.GND, MS5611_breakout.GND, Power.pin2
  5V: 1117-3_3_GND_OUT_IN.IN, C2.+, I2C_Level_Converter.HV, DC-DC.VOUT, LCD_contrast.leg2, LCD_Connector.VDD=5V, Arduino_Mini.VCC, MicroSD_breakout.+5V, RTC.5V, R10.Pin_0, Power.pin1, Keypad.pin1
  Button pad: Up.Pin_1, Up.Pin_2, Down.Pin_1, Down.Pin_2, Start/Stop.Pin_1, Start/Stop.Pin_2, Setup.Pin_1, Setup.Pin_2, R6.Pin_1, Arduino_Mini.A1, Keypad.pin2
  N1: Up.Pin_3, Up.Pin_4, R9.Pin_0
  N2: I2C_Level_Converter.TX2_LV, MS5611_breakout.SCL
  N3: I2C_Level_Converter.TX_LV, MS5611_breakout.SDA
  N4: I2C_Level_Converter.TX_HV, Arduino_Mini.A4, RTC.SDA
  N5: I2C_Level_Converter.TX2_HV, Arduino_Mini.A5, RTC.SCL
  Battery watch: DC-DC.VIN, VCC1.+, Arduino_Mini.A0, Power.pin4
  N6: Down.Pin_3, Down.Pin_4, R8.Pin_0, R9.Pin_1
  N7: Start/Stop.Pin_3, Start/Stop.Pin_4, R7.Pin_0, R8.Pin_1
  N8: Setup.Pin_3, Setup.Pin_4, R7.Pin_1, R10.Pin_1
  N9: Beeper.pin1, R12.Pin_1
  N10: LCD_contrast.wiper, LCD_Connector.VO
  N11: LCD_Connector.RS, Arduino_Mini.D9_PWM
  N12: LCD_Connector.E, Arduino_Mini.D10_PWM/SS
  N13: LCD_Connector.DB4, Arduino_Mini.D5_PWM
  N14: LCD_Connector.DB5, Arduino_Mini.D6_PWM
  N15: LCD_Connector.DB6, Arduino_Mini.D7
  N16: LCD_Connector.DB7, Arduino_Mini.D8
  N17: Arduino_Mini.D13/SCK, MicroSD_breakout.CLK
  N18: Arduino_Mini.D12/MISO, MicroSD_breakout.DO
  N19: Arduino_Mini.D11_PWM/MOSI, MicroSD_breakout.DI
  N20: Arduino_Mini.D4, MicroSD_breakout.CS
  N21: Arduino_Mini.D3_PWM, R11.Pin_0
  N22: Arduino_Mini.D2, R12.Pin_0
  N23: Mode.anode, R11.Pin_1

notes:
  AsTra V0.4, Ascend tracker, 1

custom parts:
  LCD Connector: Connect header for LCD display
  MicroSD breakout: MicroSD
  DS1307 RTC Breakout fixsize: sizefix DS1307 Real-time Clock Breakout Board with Battery
  MS5611 breakout CSG: MS5611 breakout
  MicroSD Breakout: 5V-ready microSD Breakout with Level Shifter
